// Logisim project sequential_counter.circ as structural Verilog: 2 circuits, main circuit main
module main (
  input  in_1,
  output out_2,
  output out_3,
  output out_4
);

  wire and_1_out, and_2_out, B1_qn, B_out, button_1_out, C0_qn, clock_1_out, segm_1_d, segm_1_e, segm_1_f,
       segm_1_g, segm_1_out_5, segm_1_out_6, segm_1_out_7;

  Button button_1 (.out(button_1_out));
  Clock clock_1 (.out(clock_1_out));
  D_Flip_Flop A2 (.D(B1_qn), .clk(clock_1_out), .Q(out_3), .reset(button_1_out));  // open: Qn, preset
  and and_1 (and_1_out, out_2, B1_qn);
  D_Flip_Flop B1 (.D(B_out), .clk(clock_1_out), .Q(out_4), .Qn(B1_qn), .reset(button_1_out));  // open: preset
  or B (B_out, and_1_out, and_2_out);
  and and_2 (and_2_out, C0_qn, out_3);
  D_Flip_Flop C0 (.D(out_3), .clk(clock_1_out), .Q(out_2), .Qn(C0_qn), .reset(button_1_out));  // open: preset
  SEGM segm_1 (
    .A(out_2), .B(out_4), .C(out_3), .in_4(in_1), .out_5(segm_1_out_5), .out_6(segm_1_out_6),
    .out_7(segm_1_out_7), .d(segm_1_d), .e(segm_1_e), .f(segm_1_f), .g(segm_1_g));
  _7_Segment_Display u_7_segment_display_1 (
    .g(segm_1_g), .f(segm_1_f), .a(segm_1_out_5), .b(segm_1_out_6), .e(segm_1_e), .d(segm_1_d),
    .c(segm_1_out_7));  // open: dp
endmodule

module SEGM (
  input  A,
  input  B,
  input  C,
  input  in_4,
  output out_5,
  output out_6,
  output out_7,
  output d,
  output e,
  output f,
  output g
);

  wire and_1_out, and_2_out, and_3_out, and_4_out, and_5_out, and_6_out, and_7_out, and_8_out, and_9_out,
       and_10_out, and_11_out, and_12_out, and_13_out, and_14_out, and_15_out, and_16_out, not_1_out,
       not_2_out, not_3_out;

  not not_1 (not_1_out, A);
  not not_2 (not_2_out, B);
  not not_3 (not_3_out, C);
  and and_1 (and_1_out, not_1_out, not_3_out);
  and and_2 (and_2_out, A, C);
  and and_3 (and_3_out, not_1_out, not_2_out);
  and and_4 (and_4_out, A, B);
  or or_1 (out_7, not_2_out, C, A);
  and and_5 (and_5_out, not_1_out, not_3_out);
  and and_6 (and_6_out, not_1_out, B);
  and and_7 (and_7_out, A, not_2_out, C);
  and and_8 (and_8_out, B, not_3_out);
  and and_9 (and_9_out, not_1_out, not_3_out);
  and and_10 (and_10_out, not_1_out, B);
  and and_11 (and_11_out, not_1_out, not_2_out);
  and and_12 (and_12_out, not_1_out, C);
  and and_13 (and_13_out, not_2_out, C);
  and and_14 (and_14_out, not_2_out, C);
  and and_15 (and_15_out, B, not_3_out);
  and and_16 (and_16_out, not_1_out, C);
  or or_2 (out_5, and_1_out, in_4, B, and_2_out);
  or or_3 (out_6, and_3_out, not_3_out, and_4_out);
  or or_4 (d, and_5_out, in_4, and_6_out, and_7_out, and_8_out);
  or or_5 (e, and_9_out, and_10_out);
  or or_6 (f, and_11_out, in_4, and_12_out, and_13_out);
  or or_7 (g, in_4, and_14_out, and_15_out, and_16_out);
endmodule
